// Logisim project control-logic.circ as structural Verilog: 1 circuit, main circuit control_logic
module control_logic (
  input  [31:0] Instruction,
  input  BrEq,
  input  BrLt,
  output PCSel,
  output RegWEn,
  output [2:0] ImmSel,
  output BrUn,
  output ASel,
  output BSel,
  output [3:0] ALUSel,
  output MemWEn,
  output [1:0] WBSel
);

  wire demultiplexer_1_out0, demultiplexer_1_out1, demultiplexer_1_out2, demultiplexer_1_out3, not_1_out,
       not_2_out, not_3_out, or_1_out, or_2_out, or_3_out, Plus1_out, Plus2_out;
  wire [0:0] adder_2_out, and_1_out;
  wire [2:0] priority_encoder_1_out;
  wire [5:0] adder_3_out, FinalPos, multiplexer_1_out, ROMInput;
  wire [15:14] rom_1_data;

  Demultiplexer #(.enable("false"), .select(3)) demultiplexer_1 (
    .out0(demultiplexer_1_out0), .out1(demultiplexer_1_out1), .out2(demultiplexer_1_out2),
    .out3(demultiplexer_1_out3), .in(1'b1), .sel(Instruction[6:4]));  // open: out4, out5, out6, out7
  not not_1 (not_1_out, Instruction[30]);
  not not_2 (not_2_out, Instruction[12]);
  or or_1 (or_1_out, not_1_out, not_2_out);
  ROM #(.addrWidth(6), .dataWidth(16)) rom_1 (
    .addr(ROMInput), .data({rom_1_data, WBSel, MemWEn, ALUSel, BSel, ASel, BrUn, ImmSel, RegWEn}));
  or or_2 (or_2_out, Instruction[12], Instruction[13], Instruction[14], Instruction[30], Instruction[25]);
  not not_3 (not_3_out, Instruction[13]);
  Priority_Encoder priority_encoder_1 (
    .in0(demultiplexer_1_out3), .in2(demultiplexer_1_out1), .out(priority_encoder_1_out));  // open: in1, in3, in4, in5, in6, in7, en_in, gs, en_out
  Multiplexer #(.enable("false"), .select(3), .width(6)) multiplexer_1 (
    .in0({6{1'b0}}), .in2(6'b001111), .out(multiplexer_1_out), .sel(priority_encoder_1_out));  // open: in1, in3, in4, in5, in6, in7
  or or_3 (or_3_out, Instruction[12], Instruction[13], Instruction[14], Instruction[30]);
  and Plus1 (Plus1_out, demultiplexer_1_out3, or_2_out);
  and and_1 (and_1_out[0], demultiplexer_1_out1, or_1_out, Instruction[14], not_3_out);
  and Plus2 (Plus2_out, demultiplexer_1_out3, or_3_out);
  Adder #(.width(6)) adder_1 (.a(multiplexer_1_out), .b(FinalPos), .out(ROMInput));  // open: cin, cout
  Adder #(.width(1)) adder_2 (.a(Plus2_out), .b(Plus1_out), .out(adder_2_out[0]));  // open: cin, cout
  Adder #(.width(6)) adder_3 (
    .a({{5{1'b0}}, adder_2_out[0]}), .b({3'b000, Instruction[14:12]}), .out(adder_3_out));  // open: cin, cout
  Subtractor #(.width(6)) subtractor_1 (
    .a(adder_3_out), .b({{5{1'b0}}, and_1_out[0]}), .out(FinalPos));  // open: bin, bout

  // Other names for the same wires on the sheet: Opcode[6:0] = Instruction[6:0]; Funct77thDig = Instruction[25];
  //   Funct72ndDig = Instruction[30]; Funct3[2:0] = Instruction[14:12]; Position[2:0] = Instruction[14:12]

  // Notes on the sheet:
  //   INPUTS to your circuit
  //   Connect ROM Input here ->
  //   contents of rom_1 (hex, n*v repeats v):
  //   15*0 1043 10c3 1143 1243 12c3 16c3 1343 13c3
  //   ROM FOR CONTROL LOGIC
  //   DON'T CHANGE THE LOCATIONS OF THE INPUTS AND OUTPUTS!
  //   This is only if you choose to do the ROM option
  //   CONNECT
  //   WIRE
  //   TO
  //   USE
  //   ROM
  //   OUTPUT from your circuit
  //   Reminder: If using ROM, use combinational logic for PCSel
endmodule
