// Logisim project cpu.circ as structural Verilog: 1 circuit, main circuit cpu
module cpu (
  input  clk,
  input  [31:0] Instruction,
  input  [31:0] MemReadData,
  output [31:0] MemAddress,
  output [31:0] ProgramCounter,
  output [31:0] ra,
  output [31:0] sp,
  output [31:0] t0,
  output [31:0] t1,
  output [31:0] t2,
  output [31:0] s0,
  output [31:0] s1,
  output [31:0] a0,
  output [3:0] MemWriteMask,
  output [31:0] MemWriteData
);

  wire control_logic_1_asel, control_logic_1_bsel, control_logic_1_regwen;
  wire [3:0] control_logic_1_alusel;
  wire [31:0] adder_1_out, alu_1_aluresult, imm_gen_1_immediate, multiplexer_2_out, regfile_1_regreaddata1,
       regfile_1_regreaddata2;

  Register #(.width(32)) PC (.D(adder_1_out), .clk(clk), .Q(ProgramCounter));  // open: en, clr
  Adder #(.width(32)) adder_1 (.a(ProgramCounter), .b(32'h4), .out(adder_1_out));  // open: cin, cout
  control_logic control_logic_1 (
    .RegWEn(control_logic_1_regwen), .ASel(control_logic_1_asel), .BSel(control_logic_1_bsel),
    .ALUSel(control_logic_1_alusel), .Instruction(Instruction));  // open: PCSel, ImmSel, BrUn, MemWEn, WBSel, BrEq, BrLt
  regfile regfile_1 (
    .ReadReg1(Instruction[19:15]), .ReadReg2(Instruction[24:20]), .WriteReg(Instruction[11:7]),
    .RegWriteData(alu_1_aluresult), .RegWEn(control_logic_1_regwen), .clk(clk), .ra(ra), .sp(sp), .t0(t0),
    .t1(t1), .t2(t2), .s0(s0), .s1(s1), .a0(a0), .RegReadData1(regfile_1_regreaddata1),
    .RegReadData2(regfile_1_regreaddata2));
  imm_gen imm_gen_1 (.Instruction(Instruction), .Immediate(imm_gen_1_immediate));  // open: ImmSel
  Multiplexer #(.enable("false"), .width(32)) multiplexer_1 (
    .in0(ProgramCounter), .in1(regfile_1_regreaddata1), .sel(control_logic_1_asel));  // open: out
  Multiplexer #(.enable("false"), .width(32)) multiplexer_2 (
    .in0(regfile_1_regreaddata2), .in1(imm_gen_1_immediate), .out(multiplexer_2_out),
    .sel(control_logic_1_bsel));
  alu alu_1 (.ALUResult(alu_1_aluresult), .B(multiplexer_2_out), .ALUSel(control_logic_1_alusel));  // open: A
  // branch_comp branch_comp_1: pin names not known
  // partial_store partial_store_1: pin names not known
  // partial_load partial_load_1: pin names not known
  // also tied to GND on the sheet: {control_logic_1_alusel[0], control_logic_1_alusel[1], control_logic_1_alusel[2], control_logic_1_alusel[3]}

  // Notes on the sheet:
  //   To IMEM
  //   IMEM (do **NOT** move this)
  //   From IMEM
  //   Inputs/Outputs for testing. Do **NOT** move these.
  //   It is OK to move the PC, RegFile, ALU, MEM, Branch Comp, Imm Gen, Partial Load, Partial Store and Control Logic to wherever is most convenient for you when constructing your CPU, and to delete this text
  //   To DMEM
  //   DMEM (do **NOT** move this)
  //   From DMEM
endmodule
